# Fritzing sketch powerboard_ampel2 (saved by Fritzing 0.9.3b)
circuit board: 3.54996cm x 1.18795cm

parts:
  JP2 = Header 12 [package=1x12_machine-pin-header_lock.004]
  JP4 = Header 12 [package=1x12_machine-pin-header_lock.004]
  JP3 = Header 12 [package=1x12_machine-pin-header_lock.004]
  JP1 = Header 12 [package=1x12_machine-pin-header_lock.004]

nets:
  N1: JP2.1, JP2.2, JP2.3, JP2.4, JP2.5, JP2.6, JP2.7, JP2.8, JP2.9, JP2.10, JP2.11, JP2.12
  N2: JP4.1, JP4.2, JP4.3, JP4.4, JP4.5, JP4.6, JP4.7, JP4.8, JP4.9, JP4.10, JP4.11, JP4.12
  N3: JP3.1, JP3.2, JP3.3, JP3.4, JP3.5, JP3.6, JP3.7, JP3.8, JP3.9, JP3.10, JP3.11, JP3.12
  N4: JP1.1, JP1.2, JP1.3, JP1.4, JP1.5, JP1.6, JP1.7, JP1.8, JP1.9, JP1.10, JP1.11, JP1.12
